# Fritzing sketch Garage Door (saved by Fritzing 0.9.3b)
breadboards: 1

parts:
  Componente1 = Arduino Uno (Rev3)
  R1 = Resistor [tolerance=±5% resistance=1k package=THT]
  U1 = RELAY [package=relay-g5q]
  U3 = ESP8266 WiFi Module [part_number=ESP8266]
  Q3 = npn-Powertransistor [package="TO220 [THT]"]
  Componente2 = Breadboard Power Supply Board SMD  # not connected

nets:
  N1: Componente1.D13/SCK, R1.Pin_1
  GND: Componente1.GND, U3.GND, Q3.emitter
  N2: Componente1.D2, U3.RXD
  N3: Componente1.D3_PWM, U3.TXD
  N4: Componente1.5V, U1.COIL1
  N5: R1.Pin_0, Q3.base
  N6: U1.COIL2, Q3.collector
  N7: U3.VCC, U3.CH_PD

// code stored in the sketch: Garage Door.fzz.ino
int doorControlPin = 7;

void setup() 
{
  Serial.begin(9600);
}

void loop() 
{
    digitalWrite(doorControlPin, HIGH);
    delay(600);
    digitalWrite(doorControlPin, LOW);
    delay(500000);
}
